// Logisim project anjali.circ as structural Verilog: 1 circuit, main circuit main
module main (
  input  in_1,
  input  in_2,
  input  in_3,
  input  in_4,
  input  in_5,
  input  in_6
);

  wire not_1_out;

  not not_1 (not_1_out, in_1);
  not not_2 (in_1, in_2);
  // AND_Gate and_1 has open pins: in0=in_1, in1=not_1_out, in3=in_3, in4=in_3, out=open
  // AND_Gate and_2 has open pins: in0=not_1_out, in1=in_2, in2=in_2, in3=in_4, out=open
  // AND_Gate and_3 has open pins: in0=in_1, in1=in_1, in3=in_5, out=open
  // AND_Gate and_4 has open pins: in0=in_1, in1=in_2, in3=in_6, out=open
  // OR_Gate or_1 is placed but not wired
endmodule
